# Fritzing sketch Rain_gauge_Mega_v1 (saved by Fritzing 0.9.3b)

parts:
  Part1 = Arduino Mega 2560 (Rev3)
  Part2 = Real Time Clock Module - DS1307 RTC Breakout Board
  Part3 = MicroSD Card Module
  Gauge_1 = Reed switch [package=THT]
  Gauge_2 = Reed switch [package=THT]
  Gauge_3 = Reed switch [package=THT]
  Gauge_4 = Reed switch [package=THT]
  Gauge_5 = Reed switch [package=THT]
  Gauge_6 = Reed switch [package=THT]
  Gauge_7 = Reed switch [package=THT]
  Gauge_8 = Reed switch [package=THT]
  Gauge_9 = Reed switch [package=THT]
  Gauge_10 = Reed switch [package=THT]
  Gauge_11 = Reed switch [package=THT]
  Gauge_12 = Reed switch [package=THT]
  Gauge_13 = Reed switch [package=THT]
  Gauge_14 = Reed switch [package=THT]
  Gauge_15 = Reed switch [package=THT]
  Gauge_16 = Reed switch [package=THT]
  Gauge_17 = Reed switch [package=THT]
  Gauge_18 = Reed switch [package=THT]
  Gauge_19 = Reed switch [package=THT]
  Gauge_20 = Reed switch [package=THT]
  R1 = Resistor [tolerance=±5% resistance=10k package="2512 [SMD]"]

nets:
  SCL: Part1.D21/SCL, Part1.SCL, Part2.SCL
  SDA: Part1.D20/SDA, Part1.SDA, Part2.SDA
  GND: Part1.GND, Part2.GND, Part3.GND, R1.Pin_0
  5V: Part1.5V, Part2.5V, Part3.VCC
  gauge_1: Part1.D22, Gauge_1.pin_2
  gauge_2: Part1.D23, Gauge_2.pin_2
  gauge_3: Part1.D24, Gauge_3.pin_2
  gauge_4: Part1.D25, Gauge_4.pin_2
  gauge_5: Part1.D26, Gauge_5.pin_2
  gauge_6: Part1.D27, Gauge_6.pin_2
  gauge_7: Part1.D28, Gauge_7.pin_2
  gauge_8: Part1.D29, Gauge_8.pin_2
  gauge_9: Part1.D30, Gauge_9.pin_2
  gauge_10: Part1.D31, Gauge_10.pin_2
  gauge_11: Part1.D32, Gauge_11.pin_2
  gauge_12: Part1.D33, Gauge_12.pin_2
  gauge_13: Part1.D34, Gauge_13.pin_2
  gauge_14: Part1.D35, Gauge_14.pin_2
  gauge_15: Part1.D36, Gauge_15.pin_2
  gauge_16: Part1.D37, Gauge_16.pin_2
  gauge_17: Part1.D38, Gauge_17.pin_2
  gauge_18: Part1.D39, Gauge_18.pin_2
  gauge_19: Part1.D40, Gauge_19.pin_2
  gauge_20: Part1.D41, Gauge_20.pin_2
  MISO: Part1.D50, Part3.MISO
  MOSI: Part1.D51, Part3.MOSI
  SCK: Part1.D52, Part3.SCK
  SS: Part1.D53, Part3.CS
  N1: Gauge_1.pin_1, Gauge_2.pin_1, Gauge_3.pin_1, Gauge_4.pin_1, Gauge_5.pin_1, Gauge_6.pin_1, Gauge_7.pin_1, Gauge_8.pin_1, Gauge_9.pin_1, Gauge_10.pin_1, Gauge_11.pin_1, Gauge_12.pin_1, Gauge_13.pin_1, Gauge_14.pin_1, Gauge_15.pin_1, Gauge_16.pin_1, Gauge_17.pin_1, Gauge_18.pin_1, Gauge_19.pin_1, Gauge_20.pin_1, R1.Pin_1
